# Fritzing sketch Arduino Nano NRF24 node (saved by Fritzing 0.9.3b)
breadboards: 1

parts:
  Part1 = Arduino Nano (Rev3.0)
  Part2 = NRF24L01+ Breakout Board
  LED1 = LED - 5mm [color="Blue (505nm)" package="5 mm [THT]"]
  R1 = Resistor [tolerance=±5% resistance=220 package="2512 [SMD]"]

nets:
  GND: Part1.GND, Part2.GND, R1.Pin_0
  N1: Part1.D4, LED1.anode
  N2: Part1.D9, Part2.CE
  N3: Part1.D10, Part2.CS
  N4: Part1.D11/MOSI, Part2.MOSI
  N5: Part1.D12/MISO, Part2.MISO
  3V3: Part1.3V3, Part2.VCC
  N6: Part1.D13/SCK, Part2.SCK
  N7: LED1.cathode, R1.Pin_1
