# Fritzing sketch aansluitschema (saved by Fritzing 0.9.3b)
breadboards: 2

parts:
  Onderdeel2 = Arduino Nano (Rev3.0)
  Onderdeel3 = Arduino Nano (Rev3.0)
  LED1 = smd LED [color="Blue (430nm)" package="0805 [SMD]"]
  TRRS1 = Audio Jack (TRRS) 3.5mm [part_number="LUMBERG JEITA RC-5325A" package="RC-5325A [SMD]"]  # not connected
  Onderdeel4 = MicroSD Card Module
  LED2 = smd LED [color="Red (635nm)" package="0805 [SMD]"]
  LED3 = smd LED [color="Green (565nm)" package="0805 [SMD]"]
  LED4 = smd LED [color="Orange (612nm)" package="0805 [SMD]"]
  Onderdeel5 = NRF24L01+ Breakout Board
  Onderdeel6 = RFID-RC522-v2

nets:
  GND: Onderdeel2.GND, Onderdeel3.GND, LED1.cathode, Onderdeel4.GND, Onderdeel5.GND, Onderdeel6.GND
  N1: Onderdeel2.D2, Onderdeel2.D3, LED3.anode, LED4.anode
  N2: Onderdeel2.D4, LED2.anode
  N3: Onderdeel2.D7, Onderdeel6.RST
  N4: Onderdeel2.D8, Onderdeel6.SDA
  N5: Onderdeel2.D9, Onderdeel5.CS
  N6: Onderdeel2.D10, Onderdeel5.CE
  N7: Onderdeel2.D11/MOSI, Onderdeel5.MOSI, Onderdeel6.MOSI
  N8: Onderdeel2.D12/MISO, Onderdeel5.MISO, Onderdeel6.MISO
  N9: Onderdeel2.A5, Onderdeel3.A5
  N10: Onderdeel2.A4, Onderdeel3.A4
  3V3: Onderdeel2.3V3, Onderdeel5.VCC, Onderdeel6.3.3V
  N11: Onderdeel2.D13/SCK, Onderdeel5.SCK, Onderdeel6.SCK
  N12: Onderdeel3.D2, LED1.anode
  N13: Onderdeel3.D4, Onderdeel4.CS
  N14: Onderdeel3.D11/MOSI, Onderdeel4.MOSI
  N15: Onderdeel3.D12/MISO, Onderdeel4.MISO
  3V3_2: Onderdeel3.3V3, Onderdeel4.VCC
  N16: Onderdeel3.D13/SCK, Onderdeel4.SCK
  N17: LED2.cathode, LED3.cathode, LED4.cathode

custom parts:
  RFID-RC522-v2: A simple China made RFID-RC522 Reader; do check the pin labels, as this is a MFRC522 based clone.
